# Fritzing sketch CITS (saved by Fritzing 0.9.3b)
breadboards: 1

parts:
  부품2 = Arduino Uno (Rev3)
  부품3 = LCD1602-I2C
  S1 = H-Bridge with L298N
  BT1 = Bluetooth HC-06u [package=THT]
  R1 = Resistor [tolerance=±5% resistance=220 package=THT]
  R2 = Resistor [tolerance=±5% resistance=220 package=THT]
  R3 = Resistor [tolerance=±5% resistance=220 package=THT]
  R4 = Resistor [tolerance=±5% resistance=220 package=THT]
  LED1 = LED - 5mm [color="Blue (430nm)" package="5 mm [THT]"]
  LED2 = LED - 5mm [color="Blue (430nm)" package="5 mm [THT]"]
  LED3 = LED - 5mm [color="Orange (605nm)" package="5 mm [THT]"]
  LED4 = LED - 5mm [color="Green (555nm)" package="5 mm [THT]"]
  Part1 = KY-015 Temperature & Humidity Sensor Module [package="Breakout board"]
  F1 = Fan - Ventilador [package=THT]
  F2 = Fan - Ventilador [package=THT]
  BAT1 = BC9VPC [package=bc9vpc]
  VCC1 = 4 x AAA Battery Mount

nets:
  N1: 부품2.A4/SDA, 부품3.SDA
  N2: 부품2.A5/SCL, 부품3.SCL
  N3: 부품2.D8, BT1.RXD
  N4: 부품2.D9_PWM, BT1.TXD
  N5: 부품2.D10_PWM/SS, R1.Pin_1
  N6: 부품2.D11_PWM/MOSI, R4.Pin_1
  N7: 부품2.D12/MISO, R3.Pin_1
  N8: 부품2.D13/SCK, R2.Pin_1
  N9: 부품2.D2, Part1.Vin
  N10: 부품2.D4, S1.IN1
  N11: 부품2.D5_PWM, S1.IN2
  N12: 부품2.D6_PWM, S1.IN3
  N13: 부품2.D7, S1.IN4
  VCC: 부품2.5V, 부품3.VCC, BT1.VCC, Part1.-
  GND: 부품2.GND, 부품3.GND, S1.GND, BT1.GND, LED1.cathode, LED2.cathode, LED3.cathode, LED4.cathode, Part1.S, BAT1.V-, VCC1.-
  N14: S1.12V, BAT1.V+, VCC1.+
  N15: S1.M1-01, F2.5V
  N16: S1.M1-02, F2.GND
  N17: S1.M2-01, F1.5V
  N18: S1.M2-02, F1.GND
  N19: R1.Pin_0, LED4.anode
  N20: R2.Pin_0, LED1.anode
  N21: R3.Pin_0, LED2.anode
  N22: R4.Pin_0, LED3.anode

custom parts:
  LCD1602-I2C: A standard character display, usually with 2x16 characters. Comes in many colors with LCM1602 IIC attached.
  H-Bridge with L298N: h-bridge
  Bluetooth HC-06u: Bluetooth HC-06 - face up, pins down 16.5mm x 37.5mm PCB
  KY-015 Temperature & Humidity Sensor Module: KY-015 temperature and humidity sensor module, provides a low-latency serial interface to measure humidity and temperature.
  Fan - Ventilador: Ventilador de 2 pines, se encuentra comunmente en computadoras de escritorio
